# Fritzing sketch Midir (saved by Fritzing 0.9.2b)
breadboards: 1

parts:
  Composant2 = Arduino Mega 2560 (Rev3)
  HTU21D = HTU21D Breakout
  HY-SRF05 = HY-SRF05 Ultrasonic Rangefinder
  Grove_Sound = Grove Buzz
  Grove_Light = Grove 3 Axis Digital Accelerometer 16g
  ESP8266 = ESP8266 WiFi Module
  SD_Card = LC Studio SD Card Module
  MB102 = YwRobot Breadboard Power Supply
  DS3231 = ZS-042 RTC Module

nets:
  N1: Composant2.A2, Grove_Sound.SIG
  N2: Composant2.D21/SCL, HTU21D.SDA, Grove_Light.SDA, DS3231.SDA
  N3: Composant2.D20/SDA, HTU21D.SCL, Grove_Light.SCL, DS3231.SCL
  N4: Composant2.D15/RX3, ESP8266.TXD
  N5: Composant2.D14/TX3, ESP8266.RXD
  N6: Composant2.D9_PWM, HY-SRF05.Trig
  N7: Composant2.D8_PWM, HY-SRF05.Echo
  3V3: Composant2.3V3, SD_Card.3V3
  GND: Composant2.GND, HTU21D.GND, HY-SRF05.GND, Grove_Sound.GND, Grove_Light.GND, ESP8266.GND, SD_Card.GND, MB102.GND, DS3231.GND
  VCC: Composant2.VIN, HY-SRF05.Vcc, Grove_Sound.VCC, Grove_Light.VCC, MB102.VCC#5, MB102.VCC#6
  N8: Composant2.D22, ESP8266.CH_PD
  N9: Composant2.D50, SD_Card.MISO
  N10: Composant2.D51, SD_Card.MOSI
  N11: Composant2.D52, SD_Card.SCK
  N12: Composant2.D53, SD_Card.CS
  VCC_2: HTU21D.3.3V, ESP8266.VCC, ESP8266.RST, MB102.VCC#9, MB102.VCC#10, DS3231.VCC

custom parts:
  HTU21D Breakout: This is a breadboard friendly breakout board for the Measurement Specialties high-precision, low-power digital humidity sensor.
  ESP8266 WiFi Module: Generic WiFi Module based on the ESP8266 with onboard PCB antenna and UART communications
  LC Studio SD Card Module: The LC Studio SD card module serves as an interface to an SD card. The module works at 3.3 volts and 5 volts. The SPI (Serial Peripheral Interface) protocol is used for communicating with the module.
  YwRobot Breadboard Power Supply: The YwRobot Breadboard Power Supply (MB-V2) has two power rails; they can be 5V or 3V3. Power to the module can be provided through the female USB socket or through the A10 (female) 2.1mm power jack.
